// Logisim project main.circ as structural Verilog: 1 circuit, main circuit main
module main (
);

  LED led_1 ();  // open: in
  LED led_2 ();  // open: in
  LED led_3 ();  // open: in
  // _74381 74381_1: pin names not known; wires that end beside it: 1'b1, 1'b0
  LED led_4 ();  // open: in
  LED led_5 ();  // open: in
  LED led_6 ();  // open: in
endmodule
